// Logisim project mux.circ as structural Verilog: 1 circuit, main circuit main
module main (
  input  c,
  input  b,
  input  a,
  output minority,
  output minority_2
);

  wire not_1_out;

  Multiplexer #(.select(3), .enable("false")) multiplexer_1 (
    .in0(1'b1), .in1(1'b1), .in2(1'b1), .in3(1'b0), .in4(1'b1), .in5(1'b0), .in6(1'b0), .in7(1'b0),
    .out(minority), .sel({a, b, c}));
  not not_1 (not_1_out, c);
  Multiplexer #(.select(2), .enable("false")) multiplexer_2 (
    .in0(1'b1), .in1(not_1_out), .in2(not_1_out), .in3(1'b0), .out(minority_2), .sel({a, b}));
endmodule
