// Logisim project sequential-logic.circ as structural Verilog: 2 circuits, main circuit main
module main (
  input  in_1,
  input  in_2,
  input  [7:0] in_3,
  input  enable,
  input  reset,
  input  in_6,
  output SR__prime_latch,
  output out_8,
  output [7:0] out_9
);

  wire clock_1_out, d_ff_1_q;

  Clock clock_1 (.out(clock_1_out));
  nand nand_1 (SR__prime_latch, in_1, out_8);
  nand nand_2 (out_8, SR__prime_latch, in_2);
  Register register_1 (.D(in_3), .en(enable), .Q(out_9), .clk(clock_1_out), .clr(reset));
  D_Flip_Flop d_ff_1 (.clk(clock_1_out), .D(in_6), .Q(d_ff_1_q), .en(enable), .reset(reset));  // open: Qn, preset
endmodule

module moreDemo (
  input  in_1,
  input  reset
);

  wire clock_1_out;

  Clock clock_1 (.out(clock_1_out));
  Counter counter_1 (.count(in_1), .clk(clock_1_out), .clr(reset));  // open: load, D, Q, carry
endmodule
