// Logisim project sequential-logic2.circ as structural Verilog: 2 circuits, main circuit main
module main (
  input  in_1,
  input  in_2,
  output out_3,
  output out_4,
  output q,
  output q_prime
);

  wire r_out, s_out;

  Button r (.out(r_out));
  Button s (.out(s_out));
  and and_1 (out_3, in_1, in_2);
  nor nor_1 (q, r_out, q_prime);
  nor nor_2 (q_prime, q, s_out);
  not not_1 (out_4, out_3);

  // Notes on the sheet:
  //   Combination logic: output is a function of the input
  //   Sequential logic: output is a function of input and prior output
  //   Latch: level-triggered 1 bit memory
endmodule

module moreMemory (
  input  d,
  input  [15:0] in_2,
  input  enable,
  input  reset,
  output out_5,
  output [15:0] out_6
);

  wire clock_1_out;
  wire [31:0] counter_1_q;

  Clock clock_1 (.out(clock_1_out));
  D_Flip_Flop d_ff_1 (.clk(clock_1_out), .D(d), .Q(out_5));  // open: Qn, preset, en, reset
  Register #(.width(16)) register_1 (.D(in_2), .en(enable), .Q(out_6), .clk(clock_1_out), .clr(reset));
  Counter #(.width(32), .max('hffffffff)) counter_1 (
    .Q(counter_1_q), .clk(clock_1_out));  // open: load, D, count, carry, clr
  Hex_Digit_Display hex_digit_display_1 (.value(counter_1_q[7:4]));  // open: dp
  Hex_Digit_Display hex_digit_display_2 (.value(counter_1_q[3:0]));  // open: dp
endmodule
