// Logisim project traffic-light.circ as structural Verilog: 1 circuit, main circuit main
module main (
);

  wire and_1_out, and_2_out, and_3_out, clock_1_out, nor_1_out, not_1_out, not_2_out;
  wire [1:0] or_1_out, state_q;

  Clock clock_1 (.out(clock_1_out));
  Register #(.width(2)) state (.D(or_1_out), .Q(state_q), .clk(clock_1_out));  // open: en, clr
  nor nor_1 (nor_1_out, state_q[0], state_q[1]);
  or or_1 (or_1_out[0], nor_1_out, state_q[1]);
  xor xor_1 (or_1_out[1], state_q[0], state_q[1]);
  and and_1 (and_1_out, state_q[0], not_1_out);
  LED red (.in(and_1_out));
  not not_1 (not_1_out, state_q[1]);
  and and_2 (and_2_out, state_q[1], state_q[0]);
  LED yellow (.in(and_2_out));
  not not_2 (not_2_out, state_q[0]);
  LED green (.in(and_3_out));
  and and_3 (and_3_out, not_2_out, state_q[1]);

  // Notes on the sheet:
  //   new_state
  //   10
  //   (Off) 00 -> 01 (Red)
  //   (Red) 01 -> 10 (Green)
  //   (Green) 10 -> 11 (Yellow)
  //   (Yellow) 11 -> 01 (Red)
  //   current
endmodule
