// Logisim project traffic-light2.circ as structural Verilog: 1 circuit, main circuit main
module main (
);

  wire and_1_out, and_2_out, and_3_out, and_4_out, clock_1_out, not_1_out;
  wire [1:0] or_1_out, state_q;

  Clock clock_1 (.out(clock_1_out));
  Register #(.width(2)) state (.D(or_1_out), .Q(state_q), .clk(clock_1_out));  // open: en, clr
  not not_1 (not_1_out, state_q[0]);
  and and_1 (and_1_out, state_q[1], state_q[0]);
  or or_1 (or_1_out[0], not_1_out, and_1_out);
  xor xor_1 (or_1_out[1], state_q[0], state_q[1]);
  and and_2 (and_2_out, state_q[0], ~state_q[1]);  // AND_Gate
  LED red (.in(and_2_out));
  and and_3 (and_3_out, state_q[0], state_q[1]);
  LED yellow (.in(and_3_out));
  and and_4 (and_4_out, ~state_q[0], state_q[1]);  // AND_Gate
  LED green (.in(and_4_out));

  // Notes on the sheet:
  //   current_state
  //   next_state
endmodule
