// Logisim project Lab2solution.circ as structural Verilog: 2 circuits, main circuit majority circuit
module majority_circuit (
  input  a,
  input  b,
  input  c,
  output x
);

  wire a_b_out, a_c_out, b_c_out;

  and b_c (b_c_out, b, c);
  and a_c (a_c_out, a, c);
  and a_b (a_b_out, a, b);
  or b_c___a_c___a_b (x, b_c_out, a_c_out, a_b_out);
endmodule

module adder_circuit (
  input  carryIn,
  input  a,
  input  b,
  output sum,
  output carryOut
);

  wire a_b_out, carryIn_a_b_out, carryIn_a_out, carryIn_b_out, carryIn_na_nb_out, na_2_out, na_out, nb_2_out,
       nb_out, ncarryIn_2_out, ncarryIn_a_nb_out, ncarryIn_na_b_out, ncarryIn_out;

  not ncarryIn (ncarryIn_out, a);
  not na (na_out, a);
  not ncarryIn_2 (ncarryIn_2_out, a);
  not nb (nb_out, a);
  not na_2 (na_2_out, a);
  not nb_2 (nb_2_out, a);
  and carryIn_a_b (carryIn_a_b_out, a, a, a);
  and a_b (a_b_out, a, a);
  and carryIn_b (carryIn_b_out, a, a);
  and carryIn_a (carryIn_a_out, a, a);
  and ncarryIn_na_b (ncarryIn_na_b_out, ncarryIn_out, na_out, a);
  and ncarryIn_a_nb (ncarryIn_a_nb_out, ncarryIn_2_out, a, nb_out);
  and carryIn_na_nb (carryIn_na_nb_out, a, na_2_out, nb_2_out);
  or ncarryIn_na_b___ncarryIn_a_nb___carryIn_na_nb___carryIn_a_b (sum, ncarryIn_na_b_out, ncarryIn_a_nb_out, carryIn_na_nb_out, carryIn_a_b_out);
  or a_b___carryIn_b___carryIn_a (carryOut, a_b_out, carryIn_b_out, carryIn_a_out);

  assign b = a;
  assign carryIn = a;
endmodule
