// Logisim project Lab3solution.circ as structural Verilog: 2 circuits, main circuit majority
module majority (
  input  c,
  input  a,
  input  b,
  output majority
);

  Multiplexer #(.select(2), .enable("false")) multiplexer_1 (
    .in0(1'b0), .in1(c), .in2(c), .in3(1'b1), .out(majority), .sel({b, a}));
endmodule

module full_adder (
  input  a,
  input  b,
  input  carryIn,
  output sum,
  output carryOut
);

  wire not_1_out;

  not not_1 (not_1_out, b);
  Multiplexer #(.select(2), .enable("false")) multiplexer_1 (
    .in0(b), .in1(not_1_out), .in2(not_1_out), .in3(b), .out(sum), .sel({carryIn, a}));
  Multiplexer #(.select(2), .enable("false")) multiplexer_2 (
    .in0(1'b0), .in1(b), .in2(b), .in3(1'b1), .out(carryOut), .sel({carryIn, a}));
endmodule
