// Logisim project Lab4solution.circ as structural Verilog: 2 circuits, main circuit main1
module main1 (
  input  A3,
  input  A2,
  input  A1,
  input  A0,
  output f
);

  wire and_1_out, and_2_out, and_3_out, not_1_out, not_2_out, not_3_out, not_4_out, odd_parity_1_out;

  not not_1 (not_1_out, A3);
  not not_2 (not_2_out, not_1_out);
  and and_1 (and_1_out, A2, A1);
  not not_3 (not_3_out, A1);
  not not_4 (not_4_out, A0);
  and and_2 (and_2_out, not_2_out, A2, A1, A0);
  xor odd_parity_1 (odd_parity_1_out, A3, and_1_out, A0);
  and and_3 (and_3_out, A3, A2, not_3_out, not_4_out);
  or or_1 (f, and_2_out, odd_parity_1_out, and_3_out);
endmodule

module main (
  input  A3,
  input  A2,
  input  A1,
  input  A0,
  output f
);

  wire and_1_out, and_2_out, and_3_out, xor_1_out, xor_2_out;

  and and_1 (and_1_out, ~A3, ~A2, A1, A0);  // AND_Gate
  xor xor_1 (xor_1_out, A3, A2);
  xor xor_2 (xor_2_out, A1, A0);
  and and_2 (and_2_out, A3, A2, ~A1, ~A0);  // AND_Gate
  and and_3 (and_3_out, xor_1_out, xor_2_out);
  Multiplexer #(.select(2), .enable("false")) multiplexer_1 (
    .in0(and_1_out), .in1(and_3_out), .in2(and_3_out), .in3(and_2_out), .out(f), .sel({A2, A3}));
endmodule
