// Logisim project mux.circ as structural Verilog: 1 circuit, main circuit main
module main (
  input  a,
  input  b,
  input  c,
  input  a_2,
  input  b_2,
  input  c_2,
  output minority
);

  wire c_prime_out;

  not c_prime (c_prime_out, c);
  Multiplexer #(.select(3), .enable("false")) multiplexer_1 (
    .in0(1'b1), .in1(1'b1), .in2(1'b1), .in3(1'b0), .in4(1'b1), .in5(1'b0), .in6(1'b0), .in7(1'b0),
    .sel({a_2, b_2, c_2}));  // open: out
  Multiplexer #(.select(2), .enable("false")) multiplexer_2 (
    .in0(1'b1), .in1(c_prime_out), .in2(c_prime_out), .in3(1'b0), .out(minority), .sel({a, b}));
endmodule
